# Fritzing sketch basic_led (saved by Fritzing 0.9.10b)
breadboards: 1

parts:
  Part1 = Freenove ESP32 GPIO Extension
  R1 = Resistor [tolerance=±5% power=0.25 resistance=220 package=THT]
  LED1 = LED - 5mm [color="Red (633nm)" current=0.030 package="5 mm [THT]"]
  Part2 = Freenove ESP32 WROVER [package=ESP32-WROVER]

nets:
  GND: Part1.GND, Part1.pin_82, Part1.pin_85, Part1.pin_86, Part1.pin_87, Part1.pin_88, Part1.pin_89, R1.Pin_0, Part2.GND, Part2.15, Part2.2, Part2.0, Part2.4, Part2.18, Part2.19, Part2.GND/81, Part2.3/RX, Part2.23
  N1: Part1.5V, Part1.pin_83, Part1.pin_84, Part2.6/CLK
  N2: Part1.4, LED1.anode
  N3: R1.Pin_1, LED1.cathode

custom parts:
  Freenove ESP32 GPIO Extension: WS2812B_8_LED_Ring
