# Fritzing sketch buzzer (saved by Fritzing 0.9.10b)
breadboards: 1

parts:
  ESP32 = Freenove ESP32 GPIO Extension
  Buzzer = Piezo Speaker

nets:
  N1: ESP32.GND, ESP32.pin_82, ESP32.pin_85, ESP32.pin_86, ESP32.pin_89, Buzzer.pin1
  N2: ESP32.5V, ESP32.pin_83, ESP32.pin_84
  N3: ESP32.18, Buzzer.pin2
  N4: ESP32.pin_87, ESP32.pin_88

custom parts:
  Freenove ESP32 GPIO Extension: WS2812B_8_LED_Ring
