# Fritzing sketch dht11 (saved by Fritzing 0.9.10b)
breadboards: 1

parts:
  ESP32 = Freenove ESP32 GPIO Extension
  DHT11 = Humidity and Temperature Sensor DHT11

nets:
  N1: ESP32.14, DHT11.Data-signal
  N2: ESP32.GND, ESP32.pin_82, ESP32.pin_85, ESP32.pin_86, ESP32.pin_89, DHT11.GND_2
  5V: ESP32.5V, ESP32.pin_83, ESP32.pin_84, DHT11.Vcc
  N3: ESP32.pin_87, ESP32.pin_88

notes:
  The DHT11 provided is a 3-pin version, which ignores the third pin from the left (with some additional circuitry). For this diagram, ignore the third pin from the left.

custom parts:
  Freenove ESP32 GPIO Extension: WS2812B_8_LED_Ring
  Humidity and Temperature Sensor DHT11: Digital relative humidity & temperature sensor DHT11
