# Fritzing sketch iot_demo (saved by Fritzing 0.9.10b)
breadboards: 1

parts:
  ESP32 = Freenove ESP32 GPIO Extension
  LCM1602_IIC1 = LCM1602 IIC [part_number="LCM1602 IIC" chip_label="LCM1602 IIC" package="DIP (Dual Inline) [THT]"]
  LCD1 = LCD screen
  S1 = Pushbutton [package="[THT]"]
  R1 = Resistor [tolerance=±5% power=0.25 resistance=220 package=THT]
  R2 = Resistor [tolerance=±5% power=0.25 resistance=10k package=THT]

nets:
  N1: ESP32.14, LCM1602_IIC1.SCL
  GND: ESP32.GND, ESP32.pin_82, ESP32.pin_85, ESP32.pin_86, ESP32.pin_89, LCM1602_IIC1.GND, R2.Pin_0
  N2: ESP32.13, LCM1602_IIC1.SDA
  5V: ESP32.5V, ESP32.pin_83, ESP32.pin_84, LCM1602_IIC1.VCC, S1.Pin_1, S1.Pin_2
  N3: ESP32.4, R1.Pin_0
  N4: ESP32.pin_87, ESP32.pin_88
  VSS: LCM1602_IIC1.VSS, LCD1.VSS
  VDD: LCM1602_IIC1.VDD, LCD1.VDD
  N5: LCM1602_IIC1.V0, LCD1.V0
  N6: LCM1602_IIC1.RS, LCD1.RS
  N7: LCM1602_IIC1.RW, LCD1.R/W
  N8: LCM1602_IIC1.E, LCD1.E
  N9: LCM1602_IIC1.D0, LCD1.DB0
  N10: LCM1602_IIC1.D1, LCD1.DB1
  N11: LCM1602_IIC1.D2, LCD1.DB2
  N12: LCM1602_IIC1.D3, LCD1.DB3
  N13: LCM1602_IIC1.D4, LCD1.DB4
  N14: LCM1602_IIC1.D5, LCD1.DB5
  N15: LCM1602_IIC1.D6, LCD1.DB6
  N16: LCM1602_IIC1.D7, LCD1.DB7
  N17: LCM1602_IIC1.A, LCD1.LED+
  N18: LCM1602_IIC1.K, LCD1.LED-
  N19: S1.Pin_3, S1.Pin_4, R1.Pin_1, R2.Pin_1

notes:
  The LCD in your kit already has this LCM1602 IIC adapter attached to it.
  Note: The LCM1602 IIC is already integrated LCD that came with your kit.
  This IoT Demo uses the same circuit as the Liquid Crystal Display circuit.
  This IoT demo uses the same circuit as the Liquid Crystal Display circuit.

custom parts:
  Freenove ESP32 GPIO Extension: WS2812B_8_LED_Ring
  LCM1602 IIC: I2C-Module to use a 1602 or 2004 LCD on with the wire.h libory Serial LCD Modul
