# Fritzing sketch joycon (saved by Fritzing 0.9.10b)
breadboards: 1

parts:
  ESP32 = Freenove ESP32 GPIO Extension
  Joycon = Thumb Joystick

nets:
  N1: ESP32.14, Joycon.SEL
  N2: ESP32.12, Joycon.VERT
  GND: ESP32.GND, ESP32.pin_82, ESP32.pin_85, ESP32.pin_86, ESP32.pin_89, Joycon.GND
  N3: ESP32.13, Joycon.HORZ
  5V: ESP32.5V, ESP32.pin_83, ESP32.pin_84, Joycon.VCC
  N4: ESP32.pin_87, ESP32.pin_88

custom parts:
  Freenove ESP32 GPIO Extension: WS2812B_8_LED_Ring
