# Fritzing sketch l293d_motor (saved by Fritzing 0.9.10b)
breadboards: 1

parts:
  IC1 = L293D [package=THT]
  ESP32 = Freenove ESP32 GPIO Extension
  Motor = DC Motor [voltage_(max)=6V voltage_(min)=3V]

nets:
  N1: IC1.Enable_1, ESP32.14
  N2: IC1.In_1, ESP32.27
  N3: IC1.Out_1_(_Controlled_by_Enable_1_), Motor.pin_1
  N4: IC1.0V, ESP32.GND, ESP32.pin_82, ESP32.pin_85, ESP32.pin_86, ESP32.pin_89
  N5: IC1.Out_2_(_Controlled_by_Enable_1_), Motor.pin_2
  N6: IC1.In_2, ESP32.26
  N7: IC1.+Vmotor, IC1.+V, ESP32.5V, ESP32.pin_83, ESP32.pin_84
  N8: ESP32.pin_87, ESP32.pin_88

custom parts:
  Freenove ESP32 GPIO Extension: WS2812B_8_LED_Ring
