# Fritzing sketch led_bar (saved by Fritzing 0.9.10b)
breadboards: 1

parts:
  ESP32 = Freenove ESP32 GPIO Extension
  D1 = LED_BARGRAPH_10 [package=led_bargaph_10]
  R5 = Resistor [tolerance=±5% power=0.25 resistance=220 package=THT]
  R4 = Resistor [tolerance=±5% power=0.25 resistance=220 package=THT]
  R6 = Resistor [tolerance=±5% power=0.25 resistance=220 package=THT]
  R7 = Resistor [tolerance=±5% power=0.25 resistance=220 package=THT]
  R8 = Resistor [tolerance=±5% power=0.25 resistance=220 package=THT]
  R9 = Resistor [tolerance=±5% power=0.25 resistance=220 package=THT]
  R10 = Resistor [tolerance=±5% power=0.25 resistance=220 package=THT]
  R2 = Resistor [tolerance=±5% power=0.25 resistance=220 package=THT]
  R1 = Resistor [tolerance=±5% power=0.25 resistance=220 package=THT]
  R3 = Resistor [tolerance=±5% power=0.25 resistance=220 package=THT]

nets:
  N1: ESP32.32, D1.H_A
  N2: ESP32.25, D1.F_A
  N3: ESP32.26, D1.E_A
  N4: ESP32.27, D1.D_A
  N5: ESP32.14, D1.C_A
  N6: ESP32.12, D1.B_A
  N7: ESP32.GND, ESP32.pin_82, ESP32.pin_85, ESP32.pin_86, ESP32.pin_89, R5.Pin_0, R4.Pin_0, R6.Pin_0, R7.Pin_0, R8.Pin_0, R9.Pin_0, R10.Pin_0, R2.Pin_0, R1.Pin_0, R3.Pin_0
  N8: ESP32.13, D1.A_A
  N9: ESP32.5V, ESP32.pin_83, ESP32.pin_84
  N10: ESP32.4, D1.G_A
  N11: ESP32.18, D1.I_A
  N12: ESP32.19, D1.J_A
  N13: ESP32.pin_87, ESP32.pin_88
  N14: D1.J_C, R5.Pin_1
  N15: D1.I_C, R4.Pin_1
  N16: D1.H_C, R3.Pin_1
  N17: D1.G_C, R2.Pin_1
  N18: D1.F_C, R1.Pin_1
  N19: D1.E_C, R6.Pin_1
  N20: D1.D_C, R7.Pin_1
  N21: D1.C_C, R8.Pin_1
  N22: D1.B_C, R9.Pin_1
  N23: D1.A_C, R10.Pin_1

custom parts:
  Freenove ESP32 GPIO Extension: WS2812B_8_LED_Ring
