# Fritzing sketch potentiometer (saved by Fritzing 0.9.10b)
breadboards: 1

parts:
  ESP32 = Freenove ESP32 GPIO Extension
  R1 = Rotary Potentiometer (Small) [maximum_resistance=10kΩ knob_status=50% power=0.5W package=THT]

nets:
  N1: ESP32.23#8, R1.wiper
  N2: ESP32.GND, ESP32.pin_82, ESP32.pin_85, ESP32.pin_86, ESP32.pin_89, R1.leg1
  N3: ESP32.5V, ESP32.pin_83, ESP32.pin_84
  N4: ESP32.pin_87, ESP32.pin_88, R1.leg2

custom parts:
  Freenove ESP32 GPIO Extension: WS2812B_8_LED_Ring
