# Fritzing sketch push_button_pulldown (saved by Fritzing 0.9.10b)
breadboards: 1

parts:
  ESP32 = Freenove ESP32 GPIO Extension
  S1 = Pushbutton [package="[THT]"]
  R1 = Resistor [tolerance=±5% power=0.25 resistance=10k package=THT]
  R2 = Resistor [tolerance=±5% power=0.25 resistance=220 package=THT]

nets:
  N1: ESP32.GND, ESP32.pin_82, ESP32.pin_85, ESP32.pin_86, ESP32.pin_89, R1.Pin_1
  N2: ESP32.5V, ESP32.pin_83, ESP32.pin_84, S1.Pin_1, S1.Pin_2
  N3: ESP32.4, R2.Pin_0
  N4: ESP32.pin_87, ESP32.pin_88
  N5: S1.Pin_3, S1.Pin_4, R1.Pin_0, R2.Pin_1

custom parts:
  Freenove ESP32 GPIO Extension: WS2812B_8_LED_Ring
