# Fritzing sketch push_button_pullup (saved by Fritzing 0.9.10b)
breadboards: 1

parts:
  ESP32 = Freenove ESP32 GPIO Extension
  S1 = Pushbutton [package="[THT]"]
  R1 = Resistor [tolerance=±5% power=0.25 resistance=10k package=THT]
  R2 = Resistor [tolerance=±5% power=0.25 resistance=220 package=THT]
  Part1 = Freenove ESP32 WROVER [package=ESP32-WROVER]

nets:
  GND: ESP32.GND, ESP32.pin_82, ESP32.pin_85, ESP32.pin_86, ESP32.pin_87, ESP32.pin_88, ESP32.pin_89, S1.Pin_1, S1.Pin_2, Part1.GND, Part1.15, Part1.2, Part1.0, Part1.4, Part1.18, Part1.19, Part1.GND/81, Part1.3/RX, Part1.23
  N1: ESP32.5V, ESP32.pin_83, ESP32.pin_84, R1.Pin_1, Part1.6/CLK
  N2: ESP32.4, R2.Pin_0
  N3: S1.Pin_3, S1.Pin_4, R1.Pin_0, R2.Pin_1

custom parts:
  Freenove ESP32 GPIO Extension: WS2812B_8_LED_Ring
