# Fritzing sketch rgb_led (saved by Fritzing 0.9.10b)
breadboards: 1

parts:
  Part1 = Freenove ESP32 GPIO Extension
  R2 = Rotary Potentiometer (Small) [maximum_resistance=100kΩ knob_status=50% power=0.5W package=THT]
  R3 = Rotary Potentiometer (Small) [maximum_resistance=100kΩ knob_status=50% power=0.5W package=THT]
  R1 = Rotary Potentiometer (Small) [maximum_resistance=100kΩ knob_status=50% power=0.5W package=THT]
  R4 = Resistor [tolerance=±5% power=0.25 resistance=220 package=THT]
  R5 = Resistor [tolerance=±5% power=0.25 resistance=220 package=THT]
  R6 = Resistor [tolerance=±5% power=0.25 resistance=220 package=THT]
  RGBLED = RGB LED (com. anode, rbg) [package="5 mm [THT]"]

nets:
  N1: Part1.25, R1.wiper
  N2: Part1.26, R2.wiper
  N3: Part1.27, R3.wiper
  N4: Part1.GND, Part1.pin_82, Part1.pin_85, Part1.pin_86, Part1.pin_89, R2.leg2, R3.leg2, R1.leg2
  N5: Part1.5V, Part1.pin_83, Part1.pin_84, RGBLED.common_anode
  N6: Part1.5, R6.Pin_0
  N7: Part1.18, R4.Pin_0
  N8: Part1.19, R5.Pin_0
  N9: Part1.pin_87, Part1.pin_88, R2.leg1, R3.leg1, R1.leg1
  N10: R4.Pin_1, RGBLED.blue_cathode
  N11: R5.Pin_1, RGBLED.red_cathode
  N12: R6.Pin_1, RGBLED.green_cathode

custom parts:
  Freenove ESP32 GPIO Extension: WS2812B_8_LED_Ring
