# Fritzing sketch servo (saved by Fritzing 0.9.10b)
breadboards: 1

parts:
  ESP32 = Freenove ESP32 GPIO Extension
  R1 = Rotary Potentiometer (Small) [maximum_resistance=10kΩ knob_status=50% power=0.5W package=THT]
  M1 = Dagu DGServo 9g (Top view) [part_number=RS001B]

nets:
  N1: ESP32.32, M1.pulse
  N2: ESP32.23#8, R1.wiper
  GND: ESP32.GND, ESP32.pin_82, ESP32.pin_85, ESP32.pin_86, ESP32.pin_89, R1.leg1, M1.gnd
  5V: ESP32.5V, ESP32.pin_83, ESP32.pin_84, M1.vcc
  N3: ESP32.pin_87, ESP32.pin_88, R1.leg2

custom parts:
  Freenove ESP32 GPIO Extension: WS2812B_8_LED_Ring
