# Fritzing sketch speaker (saved by Fritzing 0.9.10b)
breadboards: 1

parts:
  esp32 = Freenove ESP32 GPIO Extension
  SPKR1 = Loudspeaker
  R1 = Resistor [tolerance=±5% power=0.25 resistance=220 package=THT]

nets:
  N1: esp32.14, R1.Pin_0
  N2: esp32.GND, esp32.pin_82, esp32.pin_85, esp32.pin_86, esp32.pin_89, SPKR1.pin1
  N3: esp32.5V, esp32.pin_83, esp32.pin_84
  N4: esp32.pin_87, esp32.pin_88
  N5: SPKR1.pin2, R1.Pin_1

custom parts:
  Freenove ESP32 GPIO Extension: WS2812B_8_LED_Ring
