# Fritzing sketch ultrasonic_ranger (saved by Fritzing 0.9.10b)
breadboards: 1

parts:
  HC-SR04_Sensor_1 = HC-SR04 Ultrasonic Distance Sensor
  ESP32 = Freenove ESP32 GPIO Extension

nets:
  VCC: HC-SR04_Sensor_1.VCC, ESP32.5V, ESP32.pin_83, ESP32.pin_84
  N1: HC-SR04_Sensor_1.TRIG, ESP32.13
  N2: HC-SR04_Sensor_1.ECHO, ESP32.14
  GND: HC-SR04_Sensor_1.GND, ESP32.GND, ESP32.pin_82, ESP32.pin_85, ESP32.pin_86, ESP32.pin_89
  N3: ESP32.pin_87, ESP32.pin_88

custom parts:
  Freenove ESP32 GPIO Extension: WS2812B_8_LED_Ring
